# Fritzing sketch LED ARRAY V1_1 (saved by Fritzing 0.9.6b)
circuit board: 29.5cm x 17.6104cm
breadboards: 1

parts:
  Pad2 = Pad [width=7.9 height=9.03 connect=center]
  Pad1 = Pad [width=7.9 height=9.03 connect=center]
  U1 = Luxeon LED [package=luxeon]
  U9 = Luxeon LED [package=luxeon]
  U2 = Luxeon LED [package=luxeon]
  U16 = Luxeon LED [package=luxeon]
  U3 = Luxeon LED [package=luxeon]
  U6 = Luxeon LED [package=luxeon]
  U5 = Luxeon LED [package=luxeon]
  U4 = Luxeon LED [package=luxeon]
  U7 = Luxeon LED [package=luxeon]
  U8 = Luxeon LED [package=luxeon]
  U15 = Luxeon LED [package=luxeon]
  U14 = Luxeon LED [package=luxeon]
  U13 = Luxeon LED [package=luxeon]
  U12 = Luxeon LED [package=luxeon]
  U11 = Luxeon LED [package=luxeon]
  U28 = Luxeon LED [package=luxeon]
  U24 = Luxeon LED [package=luxeon]
  U20 = Luxeon LED [package=luxeon]
  U22 = Luxeon LED [package=luxeon]
  U30 = Luxeon LED [package=luxeon]
  U23 = Luxeon LED [package=luxeon]
  U18 = Luxeon LED [package=luxeon]
  U25 = Luxeon LED [package=luxeon]
  U32 = Luxeon LED [package=luxeon]
  U29 = Luxeon LED [package=luxeon]
  U17 = Luxeon LED [package=luxeon]
  U31 = Luxeon LED [package=luxeon]
  U19 = Luxeon LED [package=luxeon]
  U27 = Luxeon LED [package=luxeon]
  U26 = Luxeon LED [package=luxeon]
  U55 = Luxeon LED [package=luxeon]
  U44 = Luxeon LED [package=luxeon]
  U51 = Luxeon LED [package=luxeon]
  U42 = Luxeon LED [package=luxeon]
  U40 = Luxeon LED [package=luxeon]
  U57 = Luxeon LED [package=luxeon]
  U34 = Luxeon LED [package=luxeon]
  U50 = Luxeon LED [package=luxeon]
  U37 = Luxeon LED [package=luxeon]
  U39 = Luxeon LED [package=luxeon]
  U53 = Luxeon LED [package=luxeon]
  U56 = Luxeon LED [package=luxeon]
  U46 = Luxeon LED [package=luxeon]
  U59 = Luxeon LED [package=luxeon]
  U48 = Luxeon LED [package=luxeon]
  U62 = Luxeon LED [package=luxeon]
  U58 = Luxeon LED [package=luxeon]
  U45 = Luxeon LED [package=luxeon]
  U64 = Luxeon LED [package=luxeon]
  U54 = Luxeon LED [package=luxeon]
  U47 = Luxeon LED [package=luxeon]
  U35 = Luxeon LED [package=luxeon]
  U43 = Luxeon LED [package=luxeon]
  U33 = Luxeon LED [package=luxeon]
  U21 = Luxeon LED [package=luxeon]
  U63 = Luxeon LED [package=luxeon]
  U52 = Luxeon LED [package=luxeon]
  U60 = Luxeon LED [package=luxeon]
  U36 = Luxeon LED [package=luxeon]
  U49 = Luxeon LED [package=luxeon]
  U38 = Luxeon LED [package=luxeon]
  U61 = Luxeon LED [package=luxeon]
  U41 = Luxeon LED [package=luxeon]
  U109 = Luxeon LED [package=luxeon]
  U100 = Luxeon LED [package=luxeon]
  U71 = Luxeon LED [package=luxeon]
  U80 = Luxeon LED [package=luxeon]
  U86 = Luxeon LED [package=luxeon]
  U84 = Luxeon LED [package=luxeon]
  U110 = Luxeon LED [package=luxeon]
  U108 = Luxeon LED [package=luxeon]
  U72 = Luxeon LED [package=luxeon]
  U81 = Luxeon LED [package=luxeon]
  U91 = Luxeon LED [package=luxeon]
  U77 = Luxeon LED [package=luxeon]
  U76 = Luxeon LED [package=luxeon]
  U99 = Luxeon LED [package=luxeon]
  U103 = Luxeon LED [package=luxeon]
  U106 = Luxeon LED [package=luxeon]
  U90 = Luxeon LED [package=luxeon]
  U97 = Luxeon LED [package=luxeon]
  U82 = Luxeon LED [package=luxeon]
  U111 = Luxeon LED [package=luxeon]
  U96 = Luxeon LED [package=luxeon]
  U70 = Luxeon LED [package=luxeon]
  U98 = Luxeon LED [package=luxeon]
  U112 = Luxeon LED [package=luxeon]
  U83 = Luxeon LED [package=luxeon]
  U79 = Luxeon LED [package=luxeon]
  U74 = Luxeon LED [package=luxeon]
  U67 = Luxeon LED [package=luxeon]
  U102 = Luxeon LED [package=luxeon]
  U66 = Luxeon LED [package=luxeon]
  U101 = Luxeon LED [package=luxeon]
  U88 = Luxeon LED [package=luxeon]
  U89 = Luxeon LED [package=luxeon]
  U105 = Luxeon LED [package=luxeon]
  U85 = Luxeon LED [package=luxeon]
  U73 = Luxeon LED [package=luxeon]
  U104 = Luxeon LED [package=luxeon]
  U68 = Luxeon LED [package=luxeon]
  U107 = Luxeon LED [package=luxeon]
  U95 = Luxeon LED [package=luxeon]
  U92 = Luxeon LED [package=luxeon]
  U78 = Luxeon LED [package=luxeon]
  U93 = Luxeon LED [package=luxeon]
  U65 = Luxeon LED [package=luxeon]
  U94 = Luxeon LED [package=luxeon]
  U87 = Luxeon LED [package=luxeon]
  U69 = Luxeon LED [package=luxeon]
  U75 = Luxeon LED [package=luxeon]
  U10 = Luxeon LED [package=luxeon]
  R1 = Resistor [tolerance=±5% resistance=1 power=1W package="2512 [SMD]"]
  R2 = Resistor [tolerance=±5% resistance=1 power=1W package="2512 [SMD]"]
  R3 = Resistor [tolerance=±5% resistance=1 power=1W package="2512 [SMD]"]
  R4 = Resistor [tolerance=±5% resistance=1 power=1W package="2512 [SMD]"]
  R5 = Resistor [tolerance=±5% resistance=1 power=1W package="2512 [SMD]"]
  R6 = Resistor [tolerance=±5% resistance=1 power=1W package="2512 [SMD]"]
  R7 = Resistor [tolerance=±5% resistance=1 power=1W package="2512 [SMD]"]
  R8 = Resistor [tolerance=±5% resistance=1 power=1W package="2512 [SMD]"]
  R9 = Resistor [tolerance=±5% resistance=1 power=1W package="2512 [SMD]"]
  R10 = Resistor [tolerance=±5% resistance=1 power=1W package="2512 [SMD]"]
  R11 = Resistor [tolerance=±5% resistance=1 power=1W package="2512 [SMD]"]
  R12 = Resistor [tolerance=±5% resistance=1 power=1W package="2512 [SMD]"]
  R13 = Resistor [tolerance=±5% resistance=1 power=1W package="2512 [SMD]"]
  R14 = Resistor [tolerance=±5% resistance=1 power=1W package="2512 [SMD]"]
  Pad3 = Pad [width=7.9 height=9.03 connect=center]
  Pad4 = Pad [width=7.9 height=9.03 connect=center]
  LM75A = SO08 [chip_label=IC package=SO]
  V+ = female pin header, 3 pins [form="♀ (female)"]
  GND = female pin header, 3 pins [form="♀ (female)"]
  A1 = female pin header, 3 pins [form="♀ (female)"]
  R15 = Resistor [tolerance=±5% resistance=10k package="0603 [SMD]"]
  R16 = Resistor [tolerance=±5% resistance=10k package="0603 [SMD]"]
  C3 = Capacitor [package=0603-cap]
  JP1 = Header 6 [package=molex-1x6_lock]
  R17 = Resistor [tolerance=±5% resistance=10k package="0603 [SMD]"]
  A2 = female pin header, 3 pins [form="♀ (female)"]
  GND_2 = female pin header, 3 pins [form="♀ (female)"]
  VCC = female pin header, 3 pins [form="♀ (female)"]
  LM75A_2 = SO08 [chip_label=IC package=SO]
  GND_3 = female pin header, 3 pins [form="♀ (female)"]
  A3 = female pin header, 3 pins [form="♀ (female)"]
  VCC_2 = female pin header, 3 pins [form="♀ (female)"]
  GND_4 = female pin header, 3 pins [form="♀ (female)"]
  A4 = female pin header, 3 pins [form="♀ (female)"]
  VCC_3 = female pin header, 3 pins [form="♀ (female)"]
  LM75A_3 = SO08 [chip_label=IC package=SO]
  LM75A_4 = SO08 [chip_label=IC package=SO]

nets:
  N1: Pad2.pad, R1.Pin_1, R2.Pin_1, R3.Pin_1, R4.Pin_1, R5.Pin_1, R6.Pin_1, R7.Pin_1, R8.Pin_1, R9.Pin_1, R10.Pin_1, R11.Pin_1, R12.Pin_1, R13.Pin_1, R14.Pin_1, Pad3.pad
  N2: Pad1.pad, U8.A, U11.A, U25.A, U26.A, U50.A, U62.A, U33.A, U41.A, U108.A, U106.A, U112.A, U88.A, U95.A, U92.A, Pad4.pad
  N3: U1.A, U2.C
  N4: U1.C, R14.Pin_0
  N5: U9.A, U10.C
  N6: U9.C, R13.Pin_0
  N7: U2.A, U3.C
  N8: U16.A, U14.C
  N9: U16.C, U15.A
  N10: U3.A, U6.C
  N11: U6.A, U5.C
  N12: U5.A, U4.C
  N13: U4.A, U7.C
  N14: U7.A, U8.C
  N15: U15.C, U10.A
  N16: U14.A, U13.C
  N17: U13.A, U12.C
  N18: U12.A, U11.C
  N19: U28.A, U24.C
  N20: U28.C, R12.Pin_0
  N21: U24.A, U20.C
  N22: U20.A, U22.C
  N23: U22.A, U30.C
  N24: U30.A, U23.C
  N25: U23.A, U18.C
  N26: U18.A, U25.C
  N27: U32.A, U21.C
  N28: U32.C, R11.Pin_0
  N29: U29.A, U31.C
  N30: U29.C, U17.A
  N31: U17.C, U21.A
  N32: U31.A, U19.C
  N33: U19.A, U27.C
  N34: U27.A, U26.C
  N35: U55.A, U44.C
  N36: U55.C, R10.Pin_0
  N37: U44.A, U51.C
  N38: U51.A, U42.C
  N39: U42.A, U40.C
  N40: U40.A, U57.C
  N41: U57.A, U34.C
  N42: U34.A, U50.C
  N43: U37.A, U39.C
  N44: U37.C, R9.Pin_0
  N45: U39.A, U53.C
  N46: U53.A, U56.C
  N47: U56.A, U46.C
  N48: U46.A, U59.C
  N49: U59.A, U48.C
  N50: U48.A, U62.C
  N51: U58.A, U45.C
  N52: U58.C, R8.Pin_0
  N53: U45.A, U64.C
  N54: U64.A, U54.C
  N55: U54.A, U47.C
  N56: U47.A, U35.C
  N57: U35.A, U43.C
  N58: U43.A, U33.C
  N59: U63.A, U52.C
  N60: U63.C, R7.Pin_0
  N61: U52.A, U60.C
  N62: U60.A, U36.C
  N63: U36.A, U49.C
  N64: U49.A, U38.C
  N65: U38.A, U61.C
  N66: U61.A, U41.C
  N67: U109.A, U100.C
  N68: U109.C, R6.Pin_0
  N69: U100.A, U71.C
  N70: U71.A, U80.C
  N71: U80.A, U86.C
  N72: U86.A, U84.C
  N73: U84.A, U110.C
  N74: U110.A, U108.C
  N75: U72.A, U81.C
  N76: U72.C, R5.Pin_0
  N77: U81.A, U91.C
  N78: U91.A, U77.C
  N79: U77.A, U76.C
  N80: U76.A, U99.C
  N81: U99.A, U103.C
  N82: U103.A, U106.C
  N83: U90.A, U97.C
  N84: U90.C, R4.Pin_0
  N85: U97.A, U82.C
  N86: U82.A, U111.C
  N87: U111.A, U96.C
  N88: U96.A, U70.C
  N89: U70.A, U98.C
  N90: U98.A, U112.C
  N91: U83.A, U79.C
  N92: U83.C, R3.Pin_0
  N93: U79.A, U74.C
  N94: U74.A, U67.C
  N95: U67.A, U102.C
  N96: U102.A, U66.C
  N97: U66.A, U101.C
  N98: U101.A, U88.C
  N99: U89.A, U105.C
  N100: U89.C, R2.Pin_0
  N101: U105.A, U85.C
  N102: U85.A, U73.C
  N103: U73.A, U104.C
  N104: U104.A, U68.C
  N105: U68.A, U107.C
  N106: U107.A, U95.C
  N107: U92.C, U78.A
  N108: U78.C, U93.A
  N109: U93.C, U65.A
  N110: U65.C, U94.A
  N111: U94.C, U87.A
  N112: U87.C, U69.A
  N113: U69.C, U75.A
  N114: U75.C, R1.Pin_0
  N115: LM75A.1, R16.Pin_1, JP1.2, LM75A_2.1, LM75A_3.1, LM75A_4.1
  N116: LM75A.2, R15.Pin_1, JP1.3, LM75A_2.2, LM75A_3.2, LM75A_4.2
  N117: LM75A.3, JP1.4, R17.Pin_1, LM75A_2.3, LM75A_3.3, LM75A_4.3
  N118: LM75A.4, GND.pin1, GND.pin2, GND.pin3, C3.2, JP1.6, GND_2.pin1, GND_2.pin2, GND_2.pin3, LM75A_2.4, GND_3.pin1, GND_3.pin2, GND_3.pin3, GND_4.pin1, GND_4.pin2, GND_4.pin3, LM75A_3.4, LM75A_4.4
  N119: LM75A.5, A1.pin3
  N120: LM75A.6, A1.pin1
  N121: LM75A.7, A1.pin2
  N122: LM75A.8, V+.pin1, V+.pin2, V+.pin3, R15.Pin_0, R16.Pin_0, C3.1, JP1.1, R17.Pin_0, VCC.pin1, VCC.pin2, VCC.pin3, LM75A_2.8, VCC_2.pin1, VCC_2.pin2, VCC_2.pin3, VCC_3.pin1, VCC_3.pin2, VCC_3.pin3, LM75A_3.8, LM75A_4.8
  N123: A2.pin1, LM75A_2.6
  N124: A2.pin2, LM75A_2.7
  N125: A2.pin3, LM75A_2.5
  N126: A3.pin1, LM75A_4.6
  N127: A3.pin2, LM75A_4.7
  N128: A3.pin3, LM75A_4.5
  N129: A4.pin1, LM75A_3.6
  N130: A4.pin2, LM75A_3.7
  N131: A4.pin3, LM75A_3.5

notes:
  +
  -
  A1
  A0
  A2
  GND
  NC
  OS
  SDA
  VCC
  SCL
