# Fritzing sketch LED ARRAY V1_0 (saved by Fritzing 0.9.6b)
circuit board: 29.3303cm x 17.7039cm
breadboards: 1

parts:
  U28 = Luxeon LED [package=luxeon]
  R13 = Resistor [tolerance=±5% resistance=220 power=1 package="2010 [SMD]"]
  R12 = Resistor [tolerance=±5% resistance=220 power=1 package="2010 [SMD]"]
  R11 = Resistor [tolerance=±5% resistance=220 power=1 package="2010 [SMD]"]
  R10 = Resistor [tolerance=±5% resistance=220 power=1 package="2010 [SMD]"]
  R9 = Resistor [tolerance=±5% resistance=220 power=1 package="2010 [SMD]"]
  R8 = Resistor [tolerance=±5% resistance=220 power=1 package="2010 [SMD]"]
  R7 = Resistor [tolerance=±5% resistance=220 power=1 package="2010 [SMD]"]
  R6 = Resistor [tolerance=±5% resistance=220 power=1 package="2010 [SMD]"]
  R5 = Resistor [tolerance=±5% resistance=220 power=1 package="2010 [SMD]"]
  R4 = Resistor [tolerance=±5% resistance=220 power=1 package="2010 [SMD]"]
  R3 = Resistor [tolerance=±5% resistance=220 power=1 package="2010 [SMD]"]
  R2 = Resistor [tolerance=±5% resistance=220 power=1 package="2010 [SMD]"]
  R1 = Resistor [tolerance=±5% resistance=220 power=1 package="2010 [SMD]"]
  U3 = Luxeon LED [package=luxeon]
  U4 = Luxeon LED [package=luxeon]
  U5 = Luxeon LED [package=luxeon]
  U6 = Luxeon LED [package=luxeon]
  U7 = Luxeon LED [package=luxeon]
  U8 = Luxeon LED [package=luxeon]
  U11 = Luxeon LED [package=luxeon]
  U12 = Luxeon LED [package=luxeon]
  U13 = Luxeon LED [package=luxeon]
  U14 = Luxeon LED [package=luxeon]
  U15 = Luxeon LED [package=luxeon]
  U16 = Luxeon LED [package=luxeon]
  U17 = Luxeon LED [package=luxeon]
  U18 = Luxeon LED [package=luxeon]
  U19 = Luxeon LED [package=luxeon]
  U20 = Luxeon LED [package=luxeon]
  U21 = Luxeon LED [package=luxeon]
  U22 = Luxeon LED [package=luxeon]
  U23 = Luxeon LED [package=luxeon]
  U24 = Luxeon LED [package=luxeon]
  U25 = Luxeon LED [package=luxeon]
  U26 = Luxeon LED [package=luxeon]
  U27 = Luxeon LED [package=luxeon]
  U29 = Luxeon LED [package=luxeon]
  U30 = Luxeon LED [package=luxeon]
  U31 = Luxeon LED [package=luxeon]
  U32 = Luxeon LED [package=luxeon]
  U33 = Luxeon LED [package=luxeon]
  U34 = Luxeon LED [package=luxeon]
  U35 = Luxeon LED [package=luxeon]
  U36 = Luxeon LED [package=luxeon]
  U37 = Luxeon LED [package=luxeon]
  U38 = Luxeon LED [package=luxeon]
  U39 = Luxeon LED [package=luxeon]
  U40 = Luxeon LED [package=luxeon]
  U41 = Luxeon LED [package=luxeon]
  U42 = Luxeon LED [package=luxeon]
  U43 = Luxeon LED [package=luxeon]
  U44 = Luxeon LED [package=luxeon]
  U45 = Luxeon LED [package=luxeon]
  U46 = Luxeon LED [package=luxeon]
  U47 = Luxeon LED [package=luxeon]
  U48 = Luxeon LED [package=luxeon]
  U49 = Luxeon LED [package=luxeon]
  U50 = Luxeon LED [package=luxeon]
  U51 = Luxeon LED [package=luxeon]
  U52 = Luxeon LED [package=luxeon]
  U53 = Luxeon LED [package=luxeon]
  U54 = Luxeon LED [package=luxeon]
  U55 = Luxeon LED [package=luxeon]
  U56 = Luxeon LED [package=luxeon]
  U57 = Luxeon LED [package=luxeon]
  U58 = Luxeon LED [package=luxeon]
  U59 = Luxeon LED [package=luxeon]
  U60 = Luxeon LED [package=luxeon]
  U61 = Luxeon LED [package=luxeon]
  U62 = Luxeon LED [package=luxeon]
  U63 = Luxeon LED [package=luxeon]
  U64 = Luxeon LED [package=luxeon]
  U65 = Luxeon LED [package=luxeon]
  U66 = Luxeon LED [package=luxeon]
  U67 = Luxeon LED [package=luxeon]
  U68 = Luxeon LED [package=luxeon]
  U69 = Luxeon LED [package=luxeon]
  U70 = Luxeon LED [package=luxeon]
  U71 = Luxeon LED [package=luxeon]
  U72 = Luxeon LED [package=luxeon]
  U73 = Luxeon LED [package=luxeon]
  U74 = Luxeon LED [package=luxeon]
  U75 = Luxeon LED [package=luxeon]
  U76 = Luxeon LED [package=luxeon]
  U77 = Luxeon LED [package=luxeon]
  U78 = Luxeon LED [package=luxeon]
  U79 = Luxeon LED [package=luxeon]
  U80 = Luxeon LED [package=luxeon]
  U81 = Luxeon LED [package=luxeon]
  U82 = Luxeon LED [package=luxeon]
  U83 = Luxeon LED [package=luxeon]
  U84 = Luxeon LED [package=luxeon]
  U85 = Luxeon LED [package=luxeon]
  U86 = Luxeon LED [package=luxeon]
  U87 = Luxeon LED [package=luxeon]
  U88 = Luxeon LED [package=luxeon]
  U89 = Luxeon LED [package=luxeon]
  U90 = Luxeon LED [package=luxeon]
  U91 = Luxeon LED [package=luxeon]
  U92 = Luxeon LED [package=luxeon]
  U93 = Luxeon LED [package=luxeon]
  U94 = Luxeon LED [package=luxeon]
  U95 = Luxeon LED [package=luxeon]
  U96 = Luxeon LED [package=luxeon]
  U97 = Luxeon LED [package=luxeon]
  U98 = Luxeon LED [package=luxeon]
  U99 = Luxeon LED [package=luxeon]
  U100 = Luxeon LED [package=luxeon]
  U101 = Luxeon LED [package=luxeon]
  U102 = Luxeon LED [package=luxeon]
  U103 = Luxeon LED [package=luxeon]
  U104 = Luxeon LED [package=luxeon]
  U105 = Luxeon LED [package=luxeon]
  U106 = Luxeon LED [package=luxeon]
  U107 = Luxeon LED [package=luxeon]
  U108 = Luxeon LED [package=luxeon]
  U109 = Luxeon LED [package=luxeon]
  U110 = Luxeon LED [package=luxeon]
  U111 = Luxeon LED [package=luxeon]
  U112 = Luxeon LED [package=luxeon]
  Pad2 = Pad [width=7.9 height=9.03 connect=center]  # not connected
  Pad1 = Pad [width=7.9 height=9.03 connect=center]  # not connected
  U1 = Luxeon LED [package=luxeon]
  U10 = Luxeon LED [package=luxeon]
  U9 = Luxeon LED [package=luxeon]
  U2 = Luxeon LED [package=luxeon]
  R14 = Resistor [tolerance=±5% resistance=220 power=1 package="2010 [SMD]"]  # not connected

nets:
  N1: U28.A, U32.A, U37.A, U55.A, U58.A, U63.A, U72.A, U75.A, U83.A, U89.A, U90.A, U109.A
  N2: U28.C, U24.A
  N3: R13.Pin_0, U11.C
  N4: R13.Pin_1, R12.Pin_1, R11.Pin_1, R10.Pin_1, R9.Pin_1, R8.Pin_1, R7.Pin_1, R6.Pin_1, R5.Pin_1, R4.Pin_1, R3.Pin_1, R2.Pin_1, R1.Pin_1
  N5: R12.Pin_0, U25.C
  N6: R11.Pin_0, U26.C
  N7: R10.Pin_0, U50.C
  N8: R9.Pin_0, U62.C
  N9: R8.Pin_0, U33.C
  N10: R7.Pin_0, U41.C
  N11: R6.Pin_0, U108.C
  N12: R5.Pin_0, U106.C
  N13: R4.Pin_0, U112.C
  N14: R3.Pin_0, U88.C
  N15: R2.Pin_0, U95.C
  N16: R1.Pin_0, U92.C
  N17: U3.C, U6.A
  N18: U4.A, U5.C
  N19: U4.C, U7.A
  N20: U5.A, U6.C
  N21: U7.C, U8.A
  N22: U11.A, U12.C
  N23: U12.A, U13.C
  N24: U13.A, U14.C
  N25: U14.A, U16.C
  N26: U15.C, U16.A
  N27: U17.A, U21.C
  N28: U17.C, U29.A
  N29: U18.A, U23.C
  N30: U18.C, U25.A
  N31: U19.A, U31.C
  N32: U19.C, U27.A
  N33: U20.A, U24.C
  N34: U20.C, U22.A
  N35: U21.A, U32.C
  N36: U22.C, U30.A
  N37: U23.A, U30.C
  N38: U26.A, U27.C
  N39: U29.C, U31.A
  N40: U33.A, U43.C
  N41: U34.A, U57.C
  N42: U34.C, U50.A
  N43: U35.A, U47.C
  N44: U35.C, U43.A
  N45: U36.A, U60.C
  N46: U36.C, U49.A
  N47: U37.C, U39.A
  N48: U38.A, U49.C
  N49: U38.C, U61.A
  N50: U39.C, U53.A
  N51: U40.A, U42.C
  N52: U40.C, U57.A
  N53: U41.A, U61.C
  N54: U42.A, U51.C
  N55: U44.A, U55.C
  N56: U44.C, U51.A
  N57: U45.A, U58.C
  N58: U45.C, U64.A
  N59: U46.A, U56.C
  N60: U46.C, U59.A
  N61: U47.A, U54.C
  N62: U48.A, U59.C
  N63: U48.C, U62.A
  N64: U52.A, U63.C
  N65: U52.C, U60.A
  N66: U53.C, U56.A
  N67: U54.A, U64.C
  N68: U65.A, U94.C
  N69: U65.C, U93.A
  N70: U66.A, U102.C
  N71: U66.C, U101.A
  N72: U67.A, U74.C
  N73: U67.C, U102.A
  N74: U68.A, U104.C
  N75: U68.C, U107.A
  N76: U69.A, U75.C
  N77: U69.C, U87.A
  N78: U70.A, U96.C
  N79: U70.C, U98.A
  N80: U71.A, U100.C
  N81: U71.C, U80.A
  N82: U72.C, U81.A
  N83: U73.A, U85.C
  N84: U73.C, U104.A
  N85: U74.A, U79.C
  N86: U76.A, U77.C
  N87: U76.C, U99.A
  N88: U77.A, U91.C
  N89: U78.A, U93.C
  N90: U78.C, U92.A
  N91: U79.A, U83.C
  N92: U80.C, U86.A
  N93: U81.C, U91.A
  N94: U82.A, U97.C
  N95: U82.C, U111.A
  N96: U84.A, U86.C
  N97: U84.C, U110.A
  N98: U85.A, U105.C
  N99: U87.C, U94.A
  N100: U88.A, U101.C
  N101: U89.C, U105.A
  N102: U90.C, U97.A
  N103: U95.A, U107.C
  N104: U96.A, U111.C
  N105: U98.C, U112.A
  N106: U99.C, U103.A
  N107: U100.A, U109.C
  N108: U103.C, U106.A
  N109: U108.A, U110.C
  N110: U1.A, U2.C
  N111: U1.C, U9.C
  N112: U10.C, U9.A
